// Logisim project MIPS-CPU-Design-framework.circ as structural Verilog: 4 circuits, main circuit main
module main (
);

  wire Addi, AluOp1, AluOp2, ALUSrc, and_1_out, and_2_out, and_3_out, and_4_out, and_5_out, and_9_out,
       and_10_out, and_11_out, and_12_out, big, Branch, CLK, comparator_1_eq, comparator_1_gt,
       comparator_3_eq, comparator_4_eq, comparator_5_eq, comparator_6_eq, comparator_7_eq, comparator_13_eq,
       comparator_14_eq, comparator_15_eq, counter_2_q, equal, guess, Jump, MemtoReg, MemWrite, newequal,
       NEWSLT, NOP, or_1_out, Over, RegDst, RegWrite, right, RST, SLT, \small , \关卡1 , \关卡2 , \关卡3 , \存随机数 ,
       \开始 , \键盘数存在 ;
  wire [1:0] adder_4_out, multiplexer_2_out, multiplexer_3_out, multiplexer_7_out, \关卡 , \地址 ;
  wire [3:0] adder_1_out, ALUOp, bit_extender_1_out, \次数 , \次数1 , \次数2 , \次数3 ;
  wire [4:0] multiplexer_9_out, rom_1_data_2;
  wire [5:0] counter_3_q, counter_4_q, counter_5_q;
  wire [6:0] bit_extender_4_out, bit_extender_5_out, subtractor_2_out, \键盘数 ;
  wire [7:0] rom_2_data, rom_3_data, rom_4_data, rom_5_data, rom_6_data, rom_7_data, rom_8_data, rom_9_data,
       rom_10_data, rom_11_data, rom_12_data, rom_13_data, rom_14_data, rom_15_data, rom_16_data,
       rom_17_data, rom_18_data, rom_19_data, \数码管1 , \数码管2 , \数码管3 , \数码管4 , \数码管5 , \数码管6 , \数码管7 ;
  wire [31:0] adder_2_out, adder_3_out, alu_1_p5, bit_extender_2_out, bit_extender_3_out, counter_1_q,
       main_1_p4, main_1_p7, main_1_p8, multiplexer_1_out, multiplexer_4_out, multiplexer_6_out,
       multiplexer_8_out, multiplexer_11_out, multiplexer_14_out, multiplexer_15_out, multiplier_1_out,
       multiplier_2_out, PC_q, ram_1_data, rom_1_data, subtractor_1_out, \立即数 , \随机数 ;

  Button \u_总复位  (.out(RST));
  assign bit_extender_1_out = {{2{1'b0}}, \关卡 };  // Bit_Extender bit_extender_1
  Counter #(.width(32), .max('h9)) counter_1 (.Q(counter_1_q), .clk(CLK));  // open: load, D, count, carry, clr
  Counter #(.width(1), .max('h1), .ongoal("stay")) counter_2 (
    .Q(counter_2_q), .clk(\开始 ), .clr(right));  // open: load, D, count, carry
  Clock clock_1 (.out(CLK));
  Multiplier #(.width(32)) multiplier_1 (.a(\立即数 ), .b(32'h4), .out(multiplier_1_out));  // open: cin, cout
  Adder #(.width(4)) adder_1 (.a(bit_extender_1_out), .b(4'b0001), .out(adder_1_out));  // open: cin, cout
  Register #(.width(32)) register_1 (.D(counter_1_q), .Q(\随机数 ), .clk(and_1_out));  // open: en, clr
  and and_1 (and_1_out, CLK, \存随机数 );
  Button button_1 (.out(\存随机数 ));
  LED led_1 (.in(counter_2_q));
  Multiplexer #(.width(32), .enable("false")) multiplexer_1 (
    .in0(32'h4), .in1({32{1'b0}}), .out(multiplexer_1_out), .sel(Over));
  Hex_Digit_Display hex_digit_display_1 (.value(adder_1_out));  // open: dp
  Hex_Digit_Display hex_digit_display_2 (.value(\次数 ));  // open: dp
  Multiplexer #(.width(2), .enable("false")) multiplexer_2 (
    .in0(2'b00), .in1(2'b01), .out(multiplexer_2_out), .sel(\small ));
  Adder #(.width(32)) adder_2 (.a(adder_3_out), .b(multiplier_1_out), .out(adder_2_out));  // open: cin, cout
  or or_1 (or_1_out, equal, guess, newequal);
  Subtractor #(.width(32)) subtractor_1 (.a(\立即数 ), .b(32'hc00), .out(subtractor_1_out));  // open: bin, bout
  Adder #(.width(32)) adder_3 (.a(PC_q), .b(multiplexer_1_out), .out(adder_3_out));  // open: cin, cout
  _7_Segment_Display u_7_segment_display_1 (
    .g(\数码管1 [6]), .f(\数码管1 [5]), .a(\数码管1 [0]), .b(\数码管1 [1]), .e(\数码管1 [4]), .d(\数码管1 [3]), .c(\数码管1 [2]));  // open: dp
  Multiplexer #(.width(2), .enable("false")) multiplexer_3 (
    .in0(multiplexer_2_out), .in1(2'b10), .out(multiplexer_3_out), .sel(right));
  Comparator #(.width(32)) comparator_1 (.a(PC_q), .b(32'hc), .gt(comparator_1_gt), .eq(comparator_1_eq));  // open: lt
  Multiplexer #(.width(32), .enable("false")) multiplexer_4 (
    .in0(adder_3_out), .in1(adder_2_out), .out(multiplexer_4_out), .sel(and_2_out));
  and and_2 (and_2_out, or_1_out, Branch);
  Multiplier #(.width(32)) multiplier_2 (.a(subtractor_1_out), .b(32'h4), .out(multiplier_2_out));  // open: cin, cout
  _7_Segment_Display u_7_segment_display_2 (
    .g(\数码管3 [6]), .f(\数码管3 [5]), .a(\数码管3 [0]), .b(\数码管3 [1]), .e(\数码管3 [4]), .d(\数码管3 [3]), .c(\数码管3 [2]));  // open: dp
  _7_Segment_Display u_7_segment_display_3 (
    .g(\数码管2 [6]), .f(\数码管2 [5]), .a(\数码管2 [0]), .b(\数码管2 [1]), .e(\数码管2 [4]), .d(\数码管2 [3]), .c(\数码管2 [2]));  // open: dp
  Multiplexer #(.width(2), .enable("false")) multiplexer_5 (
    .in0(multiplexer_3_out), .in1(2'b11), .out(\地址 ), .sel(big));
  or or_2 (\开始 , comparator_1_gt, comparator_1_eq);
  Register #(.width(32)) PC (.D(multiplexer_6_out), .Q(PC_q), .clk(CLK), .clr(RST));  // open: en
  Multiplexer #(.width(32), .enable("false")) multiplexer_6 (
    .in0(multiplexer_4_out), .in1(multiplier_2_out), .out(multiplexer_6_out), .sel(Jump));
  _7_Segment_Display u_7_segment_display_4 (
    .g(\数码管4 [6]), .f(\数码管4 [5]), .a(\数码管4 [0]), .b(\数码管4 [1]), .e(\数码管4 [4]), .d(\数码管4 [3]), .c(\数码管4 [2]));  // open: dp
  ROM #(.addrWidth(12), .dataWidth(32)) rom_1 (
    .addr(PC_q[13:2]), .data({rom_1_data[31:26], rom_1_data_2, rom_1_data[20:0]}));  // open: sel
  Comparator #(.width(32)) comparator_2 (
    .a({32{1'b0}}), .b({rom_1_data[31:26], rom_1_data_2, rom_1_data[20:0]}), .eq(NOP));  // open: gt, lt
  Keyboard keyboard_1 (.clk(CLK), .re(and_3_out), .avail(\键盘数存在 ), .data(\键盘数 ));  // open: clr
  and and_3 (and_3_out, \键盘数存在 , Addi);
  Register #(.width(2)) register_2 (.D(adder_4_out), .Q(\关卡 ), .clk(CLK));  // open: en, clr
  Multiplexer #(.width(2), .enable("false")) multiplexer_7 (
    .in0(2'b00), .in1(2'b01), .out(multiplexer_7_out), .sel(right));
  LED led_2 (.in(NOP));
  Adder #(.width(2)) adder_4 (.a(\关卡 ), .b(multiplexer_7_out), .out(adder_4_out));  // open: cin, cout
  // Probe on rom_1_data[20:16]
  // Probe on multiplexer_8_out
  assign bit_extender_2_out = {{16{rom_1_data[15]}}, rom_1_data[15:0]};  // Bit_Extender bit_extender_2
  Multiplexer #(.width(32), .enable("false")) multiplexer_8 (
    .in0(bit_extender_2_out), .in1(bit_extender_3_out), .out(multiplexer_8_out), .sel(and_4_out));
  assign bit_extender_3_out = {{25{\键盘数 [6]}}, \键盘数 };  // Bit_Extender bit_extender_3
  and and_4 (and_4_out, \键盘数存在 , Addi);
  _7_Segment_Display u_7_segment_display_5 (
    .g(\数码管5 [6]), .f(\数码管5 [5]), .a(\数码管5 [0]), .b(\数码管5 [1]), .e(\数码管5 [4]), .d(\数码管5 [3]), .c(\数码管5 [2]));  // open: dp
  // Probe on rom_1_data_2
  Multiplexer #(.width(5), .enable("false")) multiplexer_9 (
    .in0(rom_1_data[20:16]), .in1(rom_1_data[15:11]), .out(multiplexer_9_out), .sel(RegDst));
  // Probe on rom_1_data[15:11]
  and and_5 (and_5_out, \存随机数 , Addi);
  _7_Segment_Display u_7_segment_display_6 (
    .g(\数码管7 [6]), .f(\数码管7 [5]), .a(\数码管7 [0]), .b(\数码管7 [1]), .e(\数码管7 [4]), .d(\数码管7 [3]), .c(\数码管7 [2]));  // open: dp
  _7_Segment_Display u_7_segment_display_7 (
    .g(\数码管6 [6]), .f(\数码管6 [5]), .a(\数码管6 [0]), .b(\数码管6 [1]), .e(\数码管6 [4]), .d(\数码管6 [3]), .c(\数码管6 [2]));  // open: dp
  \控制器  \u_控制器_1  (
    .ALU_OP(ALUOp), .OP(rom_1_data[31:26]), .Func(rom_1_data[5:0]), .RegWrite(RegWrite), .RegDst(RegDst),
    .AluSrc(ALUSrc), .Branch(Branch), .MemWrite(MemWrite), .MemtoReg(MemtoReg), .Aluop1(AluOp1),
    .Aluop2(AluOp2), .JUMP(Jump), .SLT(SLT), .ADDI(Addi));
  Comparator #(.width(5)) comparator_3 (.a(5'b10001), .b(rom_1_data[20:16]), .eq(comparator_3_eq));  // open: gt, lt
  Comparator #(.width(5)) comparator_4 (.a(5'b10010), .b(rom_1_data[20:16]), .eq(comparator_4_eq));  // open: gt, lt
  Comparator #(.width(5)) comparator_5 (.a(5'b10011), .b(rom_1_data[20:16]), .eq(comparator_5_eq));  // open: gt, lt
  Comparator #(.width(32)) comparator_6 (.a(32'h1), .b(main_1_p8), .eq(comparator_6_eq));  // open: gt, lt
  Multiplexer #(.width(32), .enable("false")) multiplexer_10 (
    .in0(multiplexer_8_out), .in1(\随机数 ), .out(\立即数 ), .sel(and_5_out));
  and and_6 (big, comparator_3_eq, comparator_6_eq);
  and and_7 (\small , comparator_4_eq, comparator_6_eq);
  and and_8 (right, comparator_5_eq, comparator_6_eq);
  // regfile参考设计_main main_1: pin names not known; wires that end beside it: rom_1_data_2, rom_1_data[20:16], multiplexer_9_out, main_1_p4, RegWrite, CLK, main_1_p7, main_1_p8
  // Probe on main_1_p7
  // Probe on main_1_p8
  Multiplexer #(.width(32), .enable("false")) multiplexer_11 (
    .in0(main_1_p8), .in1(\立即数 ), .out(multiplexer_11_out), .sel(ALUSrc));
  Comparator #(.width(5)) comparator_7 (.a(rom_1_data[20:16]), .b(5'b01001), .eq(comparator_7_eq));  // open: gt, lt
  and and_9 (and_9_out, comparator_7_eq, Addi);
  Bit_Extender #(.in_width(32), .out_width(7), .\type ("sign")) bit_extender_4 (
    .in(main_1_p7), .out(bit_extender_4_out));
  Bit_Extender #(.in_width(32), .out_width(7), .\type ("sign")) bit_extender_5 (
    .in(main_1_p8), .out(bit_extender_5_out));
  // ALU alu_1: pin names not known; wires that end beside it: main_1_p7, multiplexer_11_out, ALUOp, equal, alu_1_p5, alu_1_p5
  and and_10 (and_10_out, \关卡1 , and_9_out);
  and and_11 (and_11_out, \关卡2 , and_9_out);
  and and_12 (and_12_out, \关卡3 , and_9_out);
  Comparator #(.width(7)) comparator_8 (.a(bit_extender_4_out), .b(bit_extender_5_out), .eq(newequal));  // open: gt, lt
  // Probe on ALUOp
  ROM #(.addrWidth(2)) rom_2 (.addr(2'b00), .data(rom_2_data));  // open: sel
  ROM #(.addrWidth(2)) rom_3 (.addr(2'b00), .data(rom_3_data));  // open: sel
  ROM #(.addrWidth(2)) rom_4 (.addr(2'b00), .data(rom_4_data));  // open: sel
  Counter #(.width(6), .max('h5)) counter_3 (.Q(counter_3_q), .clk(and_10_out));  // open: load, D, count, carry, clr
  Counter #(.width(6), .max('h3)) counter_4 (.Q(counter_4_q), .clk(and_11_out));  // open: load, D, count, carry, clr
  Counter #(.width(6), .max('h1)) counter_5 (.Q(counter_5_q), .clk(and_12_out));  // open: load, D, count, carry, clr
  // Probe on bit_extender_5_out
  Multiplexer #(.select(2), .width(8), .enable("false")) multiplexer_12 (
    .in0({8{1'b0}}), .in1(rom_3_data), .in2(rom_4_data), .in3(rom_2_data), .out(\数码管1 ), .sel(\地址 ));
  Bit_Extender #(.in_width(6), .out_width(4)) bit_extender_6 (.in(counter_3_q), .out(\次数1 ));
  Bit_Extender #(.in_width(6), .out_width(4)) bit_extender_7 (.in(counter_4_q), .out(\次数2 ));
  Bit_Extender #(.in_width(6), .out_width(4)) bit_extender_8 (.in(counter_5_q), .out(\次数3 ));
  Multiplexer #(.select(2), .width(4), .enable("false")) multiplexer_13 (
    .in0(\次数1 ), .in1(\次数2 ), .in2(\次数3 ), .out(\次数 ), .sel(\关卡 ));  // open: in3
  Subtractor #(.width(7)) subtractor_2 (
    .a(bit_extender_5_out), .b(7'b0110000), .out(subtractor_2_out));  // open: bin, bout
  Multiplexer #(.width(32), .enable("false")) multiplexer_14 (
    .in0(alu_1_p5), .in1(ram_1_data), .out(multiplexer_14_out), .sel(MemtoReg));
  RAM #(.addrWidth(10), .dataWidth(32), .bus("separate")) ram_1 (
    .addr(alu_1_p5[11:2]), .din(main_1_p8), .data(ram_1_data), .str(MemWrite), .clk(CLK));  // open: sel, ld, clr
  ROM #(.addrWidth(2)) rom_5 (.addr(2'b00), .data(rom_5_data));  // open: sel
  ROM #(.addrWidth(2)) rom_6 (.addr(2'b00), .data(rom_6_data));  // open: sel
  ROM #(.addrWidth(2)) rom_7 (.addr(2'b00), .data(rom_7_data));  // open: sel
  Comparator #(.width(7)) comparator_9 (
    .a(subtractor_2_out), .b(bit_extender_4_out), .eq(guess), .lt(NEWSLT));  // open: gt
  Multiplexer #(.width(32), .enable("false")) multiplexer_15 (
    .in0({32{1'b0}}), .in1(32'h1), .out(multiplexer_15_out), .sel(NEWSLT));
  Multiplexer #(.select(2), .width(8), .enable("false")) multiplexer_16 (
    .in0({8{1'b0}}), .in1(rom_6_data), .in2(rom_7_data), .in3(rom_5_data), .out(\数码管2 ), .sel(\地址 ));
  Comparator #(.width(2)) comparator_10 (.a(\关卡 ), .b(2'b00), .eq(\关卡1 ));  // open: gt, lt
  Comparator #(.width(2)) comparator_11 (.a(\关卡 ), .b(2'b01), .eq(\关卡2 ));  // open: gt, lt
  Comparator #(.width(2)) comparator_12 (.a(2'b10), .b(\关卡 ), .eq(\关卡3 ));  // open: gt, lt
  Multiplexer #(.width(32), .enable("false")) multiplexer_17 (
    .in0(multiplexer_14_out), .in1(multiplexer_15_out), .out(main_1_p4), .sel(SLT));
  Comparator #(.width(4)) comparator_13 (.a(4'b0101), .b(\次数1 ), .eq(comparator_13_eq));  // open: gt, lt
  Comparator #(.width(4)) comparator_14 (.a(4'b0011), .b(\次数2 ), .eq(comparator_14_eq));  // open: gt, lt
  Comparator #(.width(4)) comparator_15 (.a(4'b0001), .b(\次数3 ), .eq(comparator_15_eq));  // open: gt, lt
  ROM #(.addrWidth(2)) rom_8 (.addr(2'b00), .data(rom_8_data));  // open: sel
  ROM #(.addrWidth(2)) rom_9 (.addr(2'b00), .data(rom_9_data));  // open: sel
  ROM #(.addrWidth(2)) rom_10 (.addr(2'b00), .data(rom_10_data));  // open: sel
  or or_3 (Over, comparator_13_eq, comparator_14_eq, comparator_15_eq);
  Multiplexer #(.select(2), .width(8), .enable("false")) multiplexer_18 (
    .in0({8{1'b0}}), .in1(rom_9_data), .in2(rom_10_data), .in3(rom_8_data), .out(\数码管3 ), .sel(\地址 ));
  ROM #(.addrWidth(2)) rom_11 (.addr(2'b00), .data(rom_11_data));  // open: sel
  ROM #(.addrWidth(2)) rom_12 (.addr(2'b00), .data(rom_12_data));  // open: sel
  ROM #(.addrWidth(2)) rom_13 (.addr(2'b00), .data(rom_13_data));  // open: sel
  Multiplexer #(.select(2), .width(8), .enable("false")) multiplexer_19 (
    .in0({8{1'b0}}), .in1(rom_12_data), .in2(rom_13_data), .in3(rom_11_data), .out(\数码管4 ), .sel(\地址 ));
  ROM #(.addrWidth(2)) rom_14 (.addr(2'b00), .data(rom_14_data));  // open: sel
  ROM #(.addrWidth(2)) rom_15 (.addr(2'b00), .data(rom_15_data));  // open: sel
  Multiplexer #(.width(8), .enable("false")) multiplexer_20 (
    .in0(rom_15_data), .in1(rom_14_data), .out(\数码管5 ), .sel(Over));
  ROM #(.addrWidth(2)) rom_16 (.addr(2'b00), .data(rom_16_data));  // open: sel
  ROM #(.addrWidth(2)) rom_17 (.addr(2'b00), .data(rom_17_data));  // open: sel
  Multiplexer #(.width(8), .enable("false")) multiplexer_21 (
    .in0(rom_17_data), .in1(rom_16_data), .out(\数码管6 ), .sel(Over));
  ROM #(.addrWidth(2)) rom_18 (.addr(2'b00), .data(rom_18_data));  // open: sel
  ROM #(.addrWidth(2)) rom_19 (.addr(2'b00), .data(rom_19_data));  // open: sel
  Multiplexer #(.width(8), .enable("false")) multiplexer_22 (
    .in0(rom_19_data), .in1(rom_18_data), .out(\数码管7 ), .sel(Over));

  // Other names for the same wires on the sheet: 过关 = right

  // Notes on the sheet:
  //   外部信号
  //   显示屏
  //   显示屏逻辑
  //   程序计数器
  //   随机数生成
  //   指令存储器
  //   contents of rom_1 (hex, n*v repeats v):
  //   20040005 20050000 10a0fffe 22060000 10c0fffe 8820 9020 9820 11240011 10a6000a a6602a 11800006
  //   20120001 22310000 22520000 22730000 21290001 8000c03 20110001 8000c0d 20130001 22310000 22520000
  //   22730000 4820 8000c01 0 0 0 8000c08
  //   指令字
  //   指令译码
  //   键盘输入
  //   rs
  //   rt
  //   rd
  //   Imm16
  //   控制器
  //   如有必要，可以修改控制器的输出端口，增加更多控制信号
  //   数据通路
  //   contents of rom_2 (hex, n*v repeats v):
  //   7c
  //   contents of rom_3 (hex, n*v repeats v):
  //   38
  //   contents of rom_4 (hex, n*v repeats v):
  //   37
  //   数据存储器
  //   contents of rom_5 (hex, n*v repeats v):
  //   6
  //   contents of rom_6 (hex, n*v repeats v):
  //   79
  //   contents of rom_7 (hex, n*v repeats v):
  //   6
  //   contents of rom_8 (hex, n*v repeats v):
  //   6f
  //   contents of rom_9 (hex, n*v repeats v):
  //   6d
  //   contents of rom_10 (hex, n*v repeats v):
  //   39
  //   contents of rom_12 (hex, n*v repeats v):
  //   6d
  //   contents of rom_13 (hex, n*v repeats v):
  //   79
  //   contents of rom_14 (hex, n*v repeats v):
  //   79
  //   contents of rom_15 (hex, n*v repeats v):
  //   31
  //   contents of rom_16 (hex, n*v repeats v):
  //   37
  //   contents of rom_17 (hex, n*v repeats v):
  //   3e
  //   contents of rom_18 (hex, n*v repeats v):
  //   5e
  //   contents of rom_19 (hex, n*v repeats v):
  //   37
endmodule

module \控制器  (
  input  [5:0] OP,
  input  [5:0] Func,
  output RegWrite,
  output RegDst,
  output AluSrc,
  output Branch,
  output MemWrite,
  output MemtoReg,
  output Aluop1,
  output Aluop2,
  output JUMP,
  output SLT,
  output ADDI,
  output [3:0] ALU_OP
);

  wire ADD, and_1_out, and_3_out, comparator_1_eq, comparator_3_eq, comparator_6_eq, comparator_7_eq,
       comparator_10_eq, MUL, not_1_out, not_2_out, not_3_out, not_4_out, not_5_out, not_6_out, not_7_out,
       not_8_out, not_9_out, not_10_out, not_11_out, not_12_out, not_13_out, not_14_out, not_15_out;

  Comparator #(.width(6)) comparator_1 (.a(OP), .b(6'b001000), .eq(comparator_1_eq));  // open: gt, lt
  Comparator #(.width(6)) comparator_2 (.a(OP), .b(6'b101011), .eq(MemWrite));  // open: gt, lt
  Comparator #(.width(6)) comparator_3 (.a(OP), .b(6'b011100), .eq(comparator_3_eq));  // open: gt, lt
  Comparator #(.width(6)) comparator_4 (.a(OP), .b(6'b100011), .eq(MemtoReg));  // open: gt, lt
  Comparator #(.width(6)) comparator_5 (.a(OP), .b(6'b000100), .eq(Aluop2));  // open: gt, lt
  Comparator #(.width(6)) comparator_6 (.a(OP), .b({6{1'b0}}), .eq(comparator_6_eq));  // open: gt, lt
  and and_1 (and_1_out, comparator_6_eq, not_15_out, not_1_out);
  not not_1 (not_1_out, ADD);
  not not_2 (not_2_out, MemWrite);
  not not_3 (not_3_out, Aluop2);
  not not_4 (not_4_out, JUMP);
  not not_5 (not_5_out, ADDI);
  not not_6 (not_6_out, MemtoReg);
  not not_7 (not_7_out, MUL);
  not not_8 (not_8_out, ADD);
  not not_9 (not_9_out, Aluop2);
  not not_10 (not_10_out, SLT);
  not not_11 (not_11_out, ADDI);
  not not_12 (not_12_out, MemWrite);
  not not_13 (not_13_out, MemtoReg);
  not not_14 (not_14_out, Aluop2);
  or or_1 (ADDI, comparator_1_eq, and_1_out);
  not not_15 (not_15_out, comparator_7_eq);
  Comparator #(.width(6)) comparator_7 (.a({6{1'b0}}), .b(Func), .eq(comparator_7_eq));  // open: gt, lt
  Comparator #(.width(6)) comparator_8 (.a(OP), .b(6'b000010), .eq(JUMP));  // open: gt, lt
  and and_2 (RegWrite, not_2_out, not_3_out, not_4_out);
  and and_3 (and_3_out, not_5_out, not_6_out);
  or or_2 (RegDst, and_3_out, SLT);
  and and_4 (AluSrc, not_7_out, not_8_out, not_9_out, not_10_out);
  and and_5 (Aluop1, not_11_out, not_12_out, not_13_out, not_14_out);
  Comparator #(.width(6)) comparator_9 (.a(Func), .b(6'b100000), .eq(ADD));  // open: gt, lt
  Comparator #(.width(6)) comparator_10 (.a(Func), .b(6'b000010), .eq(comparator_10_eq));  // open: gt, lt
  Comparator #(.width(6)) comparator_11 (.a(Func), .b(6'b101010), .eq(SLT));  // open: gt, lt
  and and_6 (MUL, comparator_3_eq, comparator_10_eq);
  Multiplexer #(.width(4), .enable("false")) multiplexer_1 (.in0(4'b0101), .in1(4'b0011), .out(ALU_OP), .sel(MUL));

  assign Branch = Aluop2;

  // Other names for the same wires on the sheet: BEQ = Aluop2; J = JUMP; LW = MemtoReg; SW = MemWrite

  // Notes on the sheet:
  //   指令译码逻辑
  //   ADDI指令：OP=8
  //   SW指令：OP=0x2b
  //   根据MIPS指令集架构定义(具体查阅教材附录A.10.3)
  //   MUL指令：OP=0x1C, Func=2
  //   ALU控制器逻辑
  //   根据此工程的ALU设计，ALU_OP=5 时执行加法，ALU_OP=3时执行乘法
endmodule

module \控制器逻辑  (
  input  MUL,
  input  ADDI,
  input  SW,
  input  LW,
  input  ADD,
  input  BEQ,
  input  J,
  input  SLT,
  output RegWrite,
  output RegDst,
  output AluSrc,
  output Branch,
  output MemWrite,
  output MemtoReg,
  output Aluop1,
  output Aluop2,
  output JUMP,
  output SLT_2,
  output ADDI_2
);

  wire and_2_out, not_1_out, not_2_out, not_3_out, not_4_out, not_5_out, not_6_out, not_7_out, not_8_out,
       not_9_out, not_10_out, not_11_out, not_12_out, not_13_out;

  not not_1 (not_1_out, SW);
  and and_1 (RegWrite, not_1_out, not_2_out, not_3_out);
  not not_2 (not_2_out, BEQ);
  not not_3 (not_3_out, J);
  not not_4 (not_4_out, ADDI);
  and and_2 (and_2_out, not_4_out, not_5_out);
  not not_5 (not_5_out, LW);
  not not_6 (not_6_out, MUL);
  not not_7 (not_7_out, ADD);
  not not_8 (not_8_out, BEQ);
  not not_9 (not_9_out, SLT);
  not not_10 (not_10_out, ADDI);
  not not_11 (not_11_out, SW);
  not not_12 (not_12_out, LW);
  not not_13 (not_13_out, BEQ);
  or or_1 (RegDst, ADDI, and_2_out);
  and and_3 (AluSrc, not_6_out, not_7_out, not_8_out, not_9_out);
  and and_4 (Aluop1, not_10_out, not_11_out, not_12_out, not_13_out);

  assign ADDI_2 = ADDI;
  assign Aluop2 = BEQ;
  assign Branch = BEQ;
  assign JUMP = J;
  assign MemtoReg = LW;
  assign MemWrite = SW;
  assign SLT_2 = SLT;
endmodule

module \显示结果  (
);

  wire [1:0] \地址 ;
  wire [7:0] rom_1_data, rom_2_data, rom_3_data, rom_4_data, rom_5_data, rom_6_data, rom_7_data, rom_8_data,
       rom_9_data, rom_10_data, rom_11_data, rom_12_data, \数码管1 , \数码管2 , \数码管3 , \数码管4 ;

  ROM #(.addrWidth(2)) rom_1 (.addr(2'b00), .data(rom_1_data));  // open: sel
  ROM #(.addrWidth(2)) rom_2 (.addr(2'b00), .data(rom_2_data));  // open: sel
  ROM #(.addrWidth(2)) rom_3 (.addr(2'b00), .data(rom_3_data));  // open: sel
  Multiplexer #(.select(2), .width(8), .enable("false")) multiplexer_1 (
    .in0(rom_1_data), .in1(rom_2_data), .in2(rom_3_data), .out(\数码管1 ), .sel(\地址 ));  // open: in3
  ROM #(.addrWidth(2)) rom_4 (.addr(2'b00), .data(rom_4_data));  // open: sel
  ROM #(.addrWidth(2)) rom_5 (.addr(2'b00), .data(rom_5_data));  // open: sel
  ROM #(.addrWidth(2)) rom_6 (.data(rom_6_data));  // open: addr, sel
  Multiplexer #(.select(2), .width(8), .enable("false")) multiplexer_2 (
    .in0(rom_4_data), .in1(rom_5_data), .in2(rom_6_data), .out(\数码管2 ), .sel(\地址 ));  // open: in3
  ROM #(.addrWidth(2)) rom_7 (.addr(2'b00), .data(rom_7_data));  // open: sel
  ROM #(.addrWidth(2)) rom_8 (.addr(2'b00), .data(rom_8_data));  // open: sel
  ROM #(.addrWidth(2)) rom_9 (.addr(2'b00), .data(rom_9_data));  // open: sel
  Multiplexer #(.select(2), .width(8), .enable("false")) multiplexer_3 (
    .in0(rom_7_data), .in1(rom_8_data), .in2(rom_9_data), .out(\数码管3 ), .sel(\地址 ));  // open: in3
  ROM #(.addrWidth(2)) rom_10 (.addr(2'b00), .data(rom_10_data));  // open: sel
  ROM #(.addrWidth(2)) rom_11 (.addr(2'b00), .data(rom_11_data));  // open: sel
  ROM #(.addrWidth(2)) rom_12 (.addr(2'b00), .data(rom_12_data));  // open: sel
  Multiplexer #(.select(2), .width(8), .enable("false")) multiplexer_4 (
    .in0(rom_10_data), .in1(rom_11_data), .in2(rom_12_data), .out(\数码管4 ), .sel(\地址 ));  // open: in3
  _7_Segment_Display u_7_segment_display_1 ();  // open: g, f, a, b, e, d, c, dp
  _7_Segment_Display u_7_segment_display_2 ();  // open: g, f, a, b, e, d, c, dp

  // Notes on the sheet:
  //   contents of rom_1 (hex, n*v repeats v):
  //   7c
  //   contents of rom_2 (hex, n*v repeats v):
  //   38
  //   contents of rom_3 (hex, n*v repeats v):
  //   37
  //   contents of rom_4 (hex, n*v repeats v):
  //   6
  //   contents of rom_5 (hex, n*v repeats v):
  //   79
  //   contents of rom_6 (hex, n*v repeats v):
  //   6
  //   contents of rom_7 (hex, n*v repeats v):
  //   6f
  //   contents of rom_8 (hex, n*v repeats v):
  //   6d
  //   contents of rom_9 (hex, n*v repeats v):
  //   39
  //   contents of rom_11 (hex, n*v repeats v):
  //   6d
  //   contents of rom_12 (hex, n*v repeats v):
  //   79
endmodule
